# Fritzing sketch MotorStepperPushButton (saved by Fritzing 0.9.3b)
breadboards: 1

parts:
  Part1 = Arduino Uno (Rev3)
  Driver2 = 28BYJ-48 Driver Module [part_number=ULN2003 package=THT]
  SM2 = 28BYJ-48 Stepper Motor [part_number=28BYJ-48]
  S1 = Momentary Switch [package=ksa_sealed_tac_switch]

nets:
  N1: Part1.D8, Driver2.IN4
  N2: Part1.D9_PWM, Driver2.IN3
  N3: Part1.D10_PWM/SS, Driver2.IN2
  N4: Part1.D11_PWM/MOSI, Driver2.IN1
  GND: Part1.GND, Driver2.GND, S1.1
  N5: Part1.D7, S1.3
  N6: Part1.5V, Driver2.Vmotor
  N7: Driver2.blue-pin, SM2.blue-pin
  N8: Driver2.pink-pin, SM2.pink-pin
  N9: Driver2.yellow-pin, SM2.yellow-pin
  N10: Driver2.orange-pin, SM2.orange-pin
  N11: Driver2.red-pin, SM2.red-pin

custom parts:
  28BYJ-48 Driver Module: Generic male header
  28BYJ-48 Stepper Motor: Unipolar Stepper Motor 28BYJ-48 Top coil - pink & orange Bottom coil - blue & yellow Common rail - red Connector pins: blue - pink - yellow - orange - red
