# Fritzing sketch SevenSegmenDisplay (saved by Fritzing 0.9.3b)
breadboards: 1

parts:
  7_Segment1 = 7 Segment Display
  R2 = Resistor [tolerance=±5% resistance=330 package=THT]
  R1 = Resistor [tolerance=±5% resistance=220 package=THT]
  Part1 = Arduino Uno (Rev3)

nets:
  N1: 7_Segment1.Segment_E, Part1.D5_PWM
  N2: 7_Segment1.common_anode, R2.Pin_0, R1.Pin_1
  N3: 7_Segment1.Segment_C, Part1.D7
  N4: 7_Segment1.Segment_B, Part1.A0
  N5: R2.Pin_1, R1.Pin_0, Part1.GND
